// Logisim project Circuito Calculadora.circ as structural Verilog: 14 circuits, main circuit main
// q
module main (
  input  [11:0] in_1,
  input  [1:0] \Selector_de_función ,
  input  Invertir_entradas,
  input  [11:0] in_4,
  output [12:0] out_5
);

  wire Complemento_a_la_base_out_3, sumador_de_12_bits_1_overflow;
  wire [11:0] Complemento_a_la_base_out_2, demultiplexer_1_out0, demultiplexer_1_out2, demultiplexer_1_out3,
       demultiplexer_2_out0, demultiplexer_2_out1, demultiplexer_2_out3, multiplexer_1_out,
       multiplexer_2_out, multiplexer_3_out, multiplexer_4_out, multiplexer_5_out, sumador_de_12_bits_1_out_4;

  Multiplexer #(.width(12)) multiplexer_1 (
    .in0(in_1), .in1(in_4), .out(multiplexer_1_out), .sel(Invertir_entradas), .en(1'b1));
  Demultiplexer #(.select(2), .width(12)) demultiplexer_1 (
    .out0(demultiplexer_1_out0), .out2(demultiplexer_1_out2), .out3(demultiplexer_1_out3),
    .in(multiplexer_2_out), .sel(\Selector_de_función ), .en(1'b1));  // open: out1
  Multiplexer #(.width(12)) multiplexer_2 (
    .in0(in_4), .in1(in_1), .out(multiplexer_2_out), .sel(Invertir_entradas), .en(1'b1));
  Demultiplexer #(.select(2), .width(12)) demultiplexer_2 (
    .out0(demultiplexer_2_out0), .out1(demultiplexer_2_out1), .out3(demultiplexer_2_out3),
    .in(multiplexer_1_out), .sel(\Selector_de_función ), .en(1'b1));  // open: out2
  Multiplexer #(.select(2), .width(12)) multiplexer_3 (
    .in1(demultiplexer_2_out1), .in2(demultiplexer_1_out2), .in3(demultiplexer_1_out3),
    .out(multiplexer_3_out), .sel(\Selector_de_función ), .en(1'b1));  // open: in0
  complemento_a_base_2__12_bits Complemento_a_la_base (
    .in_1(multiplexer_3_out), .out_2(Complemento_a_la_base_out_2), .out_3(Complemento_a_la_base_out_3));
  Multiplexer #(.select(2), .width(12)) multiplexer_4 (
    .in0(demultiplexer_2_out0), .in3(demultiplexer_2_out3), .out(multiplexer_4_out),
    .sel(\Selector_de_función ), .en(1'b1));  // open: in1, in2
  Multiplexer #(.select(2), .width(12)) multiplexer_5 (
    .in0(demultiplexer_1_out0), .in3(Complemento_a_la_base_out_2), .out(multiplexer_5_out),
    .sel(\Selector_de_función ), .en(1'b1));  // open: in1, in2
  sumador_de_12_bits sumador_de_12_bits_1 (
    .entrada_A(multiplexer_4_out), .entrada_B(multiplexer_5_out), .out_4(sumador_de_12_bits_1_out_4),
    .Overflow(sumador_de_12_bits_1_overflow), .in_1(1'b0));
  Multiplexer #(.select(2), .width(12)) multiplexer_6 (
    .in0(sumador_de_12_bits_1_out_4), .in1(Complemento_a_la_base_out_2), .in2(Complemento_a_la_base_out_2),
    .in3(sumador_de_12_bits_1_out_4), .out(out_5[11:0]), .sel(\Selector_de_función ), .en(1'b1));
  Multiplexer #(.select(2)) multiplexer_7 (
    .in0(sumador_de_12_bits_1_overflow), .in1(Complemento_a_la_base_out_3),
    .in2(Complemento_a_la_base_out_3), .in3(sumador_de_12_bits_1_overflow), .out(out_5[12]),
    .sel(\Selector_de_función ), .en(1'b1));
endmodule

// CSC
module sumador_completo (
  input  a,
  input  b,
  input  c,
  output s__carreo,
  output r__resultado
);

  wire a_b_c_out, a_b_prime_c_prime_out, a_prime_b_c_prime_out, a_prime_b_prime_c_out, ab_out, ac_out,
       bc_out, not_1_out, not_2_out, not_3_out;

  not not_1 (not_1_out, a);
  not not_2 (not_2_out, b);
  not not_3 (not_3_out, c);
  or ab (ab_out, a, b);
  or bc (bc_out, b, c);
  or ac (ac_out, a, c);
  or a_b_c (a_b_c_out, a, b, c);
  or a_prime_b_c_prime (a_prime_b_c_prime_out, not_1_out, b, not_3_out);
  or a_b_prime_c_prime (a_b_prime_c_prime_out, a, not_2_out, not_3_out);
  or a_prime_b_prime_c (a_prime_b_prime_c_out, not_1_out, not_2_out, c);
  and and_1 (s__carreo, ab_out, bc_out, ac_out);
  and and_2 (r__resultado, a_b_c_out, a_prime_b_c_prime_out, a_b_prime_c_prime_out, a_prime_b_prime_c_out);
endmodule

module complemento_a_base_2__12_bits (
  input  [11:0] in_1,
  output [11:0] out_2,
  output out_3
);

  wire [11:0] not_1_out;

  not not_1 (not_1_out[0], in_1[0]);
  not not_2 (not_1_out[1], in_1[1]);
  not not_3 (not_1_out[2], in_1[2]);
  not not_4 (not_1_out[3], in_1[3]);
  not not_5 (not_1_out[4], in_1[4]);
  not not_6 (not_1_out[5], in_1[5]);
  not not_7 (not_1_out[6], in_1[6]);
  not not_8 (not_1_out[7], in_1[7]);
  not not_9 (not_1_out[8], in_1[8]);
  not not_10 (not_1_out[9], in_1[9]);
  not not_11 (not_1_out[10], in_1[10]);
  not not_12 (not_1_out[11], in_1[11]);
  sumador_de_12_bits sumador_de_12_bits_1 (
    .entrada_A(not_1_out), .entrada_B(12'h1), .out_4(out_2), .Overflow(out_3), .in_1(1'b0));
endmodule

module sumador_de_12_bits (
  input  in_1,
  input  [11:0] entrada_A,
  input  [11:0] entrada_B,
  output [11:0] out_4,
  output Overflow
);

  wire sumador_completo_1_s__carreo, sumador_completo_2_s__carreo, sumador_completo_3_s__carreo,
       sumador_completo_4_s__carreo, sumador_completo_5_s__carreo, sumador_completo_6_s__carreo,
       sumador_completo_7_s__carreo, sumador_completo_8_s__carreo, sumador_completo_9_s__carreo,
       sumador_completo_10_s__carreo, sumador_completo_11_s__carreo;

  sumador_completo sumador_completo_1 (
    .a(entrada_A[0]), .b(entrada_B[0]), .c(in_1), .s__carreo(sumador_completo_1_s__carreo),
    .r__resultado(out_4[0]));
  sumador_completo sumador_completo_2 (
    .a(entrada_A[1]), .b(entrada_B[1]), .c(sumador_completo_1_s__carreo),
    .s__carreo(sumador_completo_2_s__carreo), .r__resultado(out_4[1]));
  sumador_completo sumador_completo_3 (
    .a(entrada_A[2]), .b(entrada_B[2]), .c(sumador_completo_2_s__carreo),
    .s__carreo(sumador_completo_3_s__carreo), .r__resultado(out_4[2]));
  sumador_completo sumador_completo_4 (
    .a(entrada_A[3]), .b(entrada_B[3]), .c(sumador_completo_3_s__carreo),
    .s__carreo(sumador_completo_4_s__carreo), .r__resultado(out_4[3]));
  sumador_completo sumador_completo_5 (
    .a(entrada_A[4]), .b(entrada_B[4]), .c(sumador_completo_4_s__carreo),
    .s__carreo(sumador_completo_5_s__carreo), .r__resultado(out_4[4]));
  sumador_completo Sumador_completo_de_dos_bits ();  // open: a, b, c, s__carreo, r__resultado
  sumador_completo sumador_completo_6 (
    .a(entrada_A[5]), .b(entrada_B[5]), .c(sumador_completo_5_s__carreo),
    .s__carreo(sumador_completo_6_s__carreo), .r__resultado(out_4[5]));
  sumador_completo sumador_completo_7 (
    .a(entrada_A[6]), .b(entrada_B[6]), .c(sumador_completo_6_s__carreo),
    .s__carreo(sumador_completo_7_s__carreo), .r__resultado(out_4[6]));
  sumador_completo sumador_completo_8 (
    .a(entrada_A[7]), .b(entrada_B[7]), .c(sumador_completo_7_s__carreo),
    .s__carreo(sumador_completo_8_s__carreo), .r__resultado(out_4[7]));
  sumador_completo sumador_completo_9 (
    .a(entrada_A[8]), .b(entrada_B[8]), .c(sumador_completo_8_s__carreo),
    .s__carreo(sumador_completo_9_s__carreo), .r__resultado(out_4[8]));
  sumador_completo sumador_completo_10 (
    .a(entrada_A[9]), .b(entrada_B[9]), .c(sumador_completo_9_s__carreo),
    .s__carreo(sumador_completo_10_s__carreo), .r__resultado(out_4[9]));
  sumador_completo sumador_completo_11 (
    .a(entrada_A[10]), .b(entrada_B[10]), .c(sumador_completo_10_s__carreo),
    .s__carreo(sumador_completo_11_s__carreo), .r__resultado(out_4[10]));
  sumador_completo sumador_completo_12 (
    .a(entrada_A[11]), .b(entrada_B[11]), .c(sumador_completo_11_s__carreo), .s__carreo(Overflow),
    .r__resultado(out_4[11]));

  // Notes on the sheet:
  //   carreo 
  //   carreo 
  //   resultado
endmodule

module Sol_parte_1 (
  input  in_1,
  input  [11:0] in_2,
  input  in_3,
  input  [11:0] in_4,
  output [11:0] out_5,
  output Overflow_de_la_suma
);

  wire not_1_out, not_2_out;
  wire [11:0] Complemento_a_la_base_2_out_2, Complemento_a_la_base_out_2, controlled_buffer_1_out,
       controlled_buffer_2_out;

  not not_1 (not_1_out, in_1);
  assign controlled_buffer_1_out = not_1_out ? in_2 : 12'bz;  // Controlled_Buffer controlled_buffer_1
  not not_2 (not_2_out, in_3);
  assign controlled_buffer_2_out = not_2_out ? in_4 : 12'bz;  // Controlled_Buffer controlled_buffer_2
  complemento_a_base_2__12_bits Complemento_a_la_base (
    .in_1(in_2), .out_2(Complemento_a_la_base_out_2));  // open: out_3
  complemento_a_base_2__12_bits Complemento_a_la_base_2 (
    .in_1(in_4), .out_2(Complemento_a_la_base_2_out_2));  // open: out_3
  assign controlled_buffer_1_out = in_1 ? Complemento_a_la_base_out_2 : 12'bz;  // Controlled_Buffer controlled_buffer_3
  assign controlled_buffer_2_out = in_3 ? Complemento_a_la_base_2_out_2 : 12'bz;  // Controlled_Buffer controlled_buffer_4
  sumador_de_12_bits Sumador_12_bits (
    .entrada_A(controlled_buffer_1_out), .entrada_B(controlled_buffer_2_out), .out_4(out_5),
    .Overflow(Overflow_de_la_suma), .in_1(1'b0));
endmodule

module comparador (
  input  [11:0] in_1,
  input  [11:0] in_2,
  output A__B,
  output A__B_2,
  output A_B
);

  wire and_1_out, and_2_out, controlled_buffer_1_out, not_1_out, not_2_out, not_4_out, todos_seros_out;
  wire [11:0] complemento_a_base_2_12_bits_1_out_2, sumador_de_12_bits_1_out_4;

  sumador_de_12_bits sumador_de_12_bits_1 (
    .entrada_A(in_1), .entrada_B(complemento_a_base_2_12_bits_1_out_2), .out_4(sumador_de_12_bits_1_out_4),
    .in_1(1'b0));  // open: Overflow
  complemento_a_base_2__12_bits complemento_a_base_2_12_bits_1 (
    .in_1(in_2), .out_2(complemento_a_base_2_12_bits_1_out_2));  // open: out_3
  not not_1 (not_1_out, in_2[11]);
  and and_1 (and_1_out, sumador_de_12_bits_1_out_4[11], in_1[11], not_1_out);
  or todos_seros (todos_seros_out, sumador_de_12_bits_1_out_4[0], sumador_de_12_bits_1_out_4[1], sumador_de_12_bits_1_out_4[2], sumador_de_12_bits_1_out_4[3], sumador_de_12_bits_1_out_4[4], sumador_de_12_bits_1_out_4[5], sumador_de_12_bits_1_out_4[6], sumador_de_12_bits_1_out_4[7], sumador_de_12_bits_1_out_4[8], sumador_de_12_bits_1_out_4[9], sumador_de_12_bits_1_out_4[10], sumador_de_12_bits_1_out_4[11]);
  and and_2 (and_2_out, and_1_out, todos_seros_out);
  not not_2 (not_2_out, and_2_out);
  assign controlled_buffer_1_out = not_2_out ? sumador_de_12_bits_1_out_4[11] : 1'bz;  // Controlled_Buffer controlled_buffer_1
  assign controlled_buffer_1_out = and_2_out ? ~sumador_de_12_bits_1_out_4[11] : 1'bz;  // Controlled_Inverter controlled_inverter_1
  not not_3 (A__B, todos_seros_out);
  not not_4 (not_4_out, A__B);
  assign A__B_2 = not_4_out ? controlled_buffer_1_out : 1'bz;  // Controlled_Buffer controlled_buffer_2
  not not_5 (A_B, A__B_2);
endmodule

module circuito_parte_2 (
  input  [11:0] in_1,
  input  [1:0] \Selector_de_función ,
  input  Invertir_entradas,
  input  [11:0] in_4,
  output [12:0] out_5
);

  wire Complemento_a_la_base_out_3, sumador_de_12_bits_1_overflow;
  wire [11:0] Complemento_a_la_base_out_2, demultiplexer_1_out0, demultiplexer_1_out2, demultiplexer_1_out3,
       demultiplexer_2_out0, demultiplexer_2_out1, demultiplexer_2_out3, multiplexer_1_out,
       multiplexer_2_out, multiplexer_3_out, multiplexer_4_out, multiplexer_5_out, sumador_de_12_bits_1_out_4;

  Multiplexer #(.width(12)) multiplexer_1 (
    .in0(in_1), .in1(in_4), .out(multiplexer_1_out), .sel(Invertir_entradas), .en(1'b1));
  Multiplexer #(.width(12)) multiplexer_2 (
    .in0(in_4), .in1(in_1), .out(multiplexer_2_out), .sel(Invertir_entradas), .en(1'b1));
  Demultiplexer #(.select(2), .width(12)) demultiplexer_1 (
    .out0(demultiplexer_1_out0), .out2(demultiplexer_1_out2), .out3(demultiplexer_1_out3),
    .in(multiplexer_2_out), .sel(\Selector_de_función ), .en(1'b1));  // open: out1
  Demultiplexer #(.select(2), .width(12)) demultiplexer_2 (
    .out0(demultiplexer_2_out0), .out1(demultiplexer_2_out1), .out3(demultiplexer_2_out3),
    .in(multiplexer_1_out), .sel(\Selector_de_función ), .en(1'b1));  // open: out2
  Multiplexer #(.select(2), .width(12)) multiplexer_3 (
    .in1(demultiplexer_2_out1), .in2(demultiplexer_1_out2), .in3(demultiplexer_1_out3),
    .out(multiplexer_3_out), .sel(\Selector_de_función ), .en(1'b1));  // open: in0
  complemento_a_base_2__12_bits Complemento_a_la_base (
    .in_1(multiplexer_3_out), .out_2(Complemento_a_la_base_out_2), .out_3(Complemento_a_la_base_out_3));
  Multiplexer #(.select(2), .width(12)) multiplexer_4 (
    .in0(demultiplexer_2_out0), .in3(demultiplexer_2_out3), .out(multiplexer_4_out),
    .sel(\Selector_de_función ), .en(1'b1));  // open: in1, in2
  Multiplexer #(.select(2), .width(12)) multiplexer_5 (
    .in0(demultiplexer_1_out0), .in3(Complemento_a_la_base_out_2), .out(multiplexer_5_out),
    .sel(\Selector_de_función ), .en(1'b1));  // open: in1, in2
  sumador_de_12_bits sumador_de_12_bits_1 (
    .entrada_A(multiplexer_4_out), .entrada_B(multiplexer_5_out), .out_4(sumador_de_12_bits_1_out_4),
    .Overflow(sumador_de_12_bits_1_overflow), .in_1(1'b0));
  Multiplexer #(.select(2), .width(12)) multiplexer_6 (
    .in0(sumador_de_12_bits_1_out_4), .in1(Complemento_a_la_base_out_2), .in2(Complemento_a_la_base_out_2),
    .in3(sumador_de_12_bits_1_out_4), .out(out_5[11:0]), .sel(\Selector_de_función ), .en(1'b1));
  Multiplexer #(.select(2)) multiplexer_7 (
    .in0(sumador_de_12_bits_1_overflow), .in1(Complemento_a_la_base_out_3),
    .in2(Complemento_a_la_base_out_3), .in3(sumador_de_12_bits_1_overflow), .out(out_5[12]),
    .sel(\Selector_de_función ), .en(1'b1));
endmodule

module circuito_final (
  input  [11:0] in_1,
  input  [2:0] \Selector_de_función ,
  input  Invertir_entradas,
  input  [11:0] in_4,
  output [12:0] Salida_C,
  output [11:0] Salida_D
);

  wire Comparador_a__b, Comparador_a__b_2, Comparador_a_b, Complemento_a_la_base_out_3,
       decodificador_7_segmentos_1_a, decodificador_7_segmentos_1_b, decodificador_7_segmentos_1_c,
       decodificador_7_segmentos_1_d, decodificador_7_segmentos_1_e, decodificador_7_segmentos_1_f,
       decodificador_7_segmentos_1_g, decodificador_7_segmentos_2_a, decodificador_7_segmentos_2_b,
       decodificador_7_segmentos_2_c, decodificador_7_segmentos_2_d, decodificador_7_segmentos_2_e,
       decodificador_7_segmentos_2_f, decodificador_7_segmentos_2_g, decodificador_7_segmentos_3_a,
       decodificador_7_segmentos_3_b, decodificador_7_segmentos_3_c, decodificador_7_segmentos_3_d,
       decodificador_7_segmentos_3_e, decodificador_7_segmentos_3_f, decodificador_7_segmentos_3_g,
       decodificador_7_segmentos_4_a, decodificador_7_segmentos_4_b, decodificador_7_segmentos_4_c,
       decodificador_7_segmentos_4_d, decodificador_7_segmentos_4_e, decodificador_7_segmentos_4_f,
       decodificador_7_segmentos_4_g, decodificador_7_segmentos_5_a, decodificador_7_segmentos_5_b,
       decodificador_7_segmentos_5_c, decodificador_7_segmentos_5_d, decodificador_7_segmentos_5_e,
       decodificador_7_segmentos_5_f, decodificador_7_segmentos_5_g, decodificador_7_segmentos_6_a,
       decodificador_7_segmentos_6_b, decodificador_7_segmentos_6_c, decodificador_7_segmentos_6_d,
       decodificador_7_segmentos_6_e, decodificador_7_segmentos_6_f, decodificador_7_segmentos_6_g,
       decodificador_7_segmentos_7_a, decodificador_7_segmentos_7_b, decodificador_7_segmentos_7_c,
       decodificador_7_segmentos_7_d, decodificador_7_segmentos_7_e, decodificador_7_segmentos_7_f,
       decodificador_7_segmentos_7_g, decodificador_7_segmentos_8_a, decodificador_7_segmentos_8_b,
       decodificador_7_segmentos_8_c, decodificador_7_segmentos_8_d, decodificador_7_segmentos_8_e,
       decodificador_7_segmentos_8_f, decodificador_7_segmentos_8_g, decodificador_7_segmentos_9_a,
       decodificador_7_segmentos_9_b, decodificador_7_segmentos_9_c, decodificador_7_segmentos_9_d,
       decodificador_7_segmentos_9_e, decodificador_7_segmentos_9_f, decodificador_7_segmentos_9_g,
       decodificador_7_segmentos_10_a, decodificador_7_segmentos_10_b, decodificador_7_segmentos_10_c,
       decodificador_7_segmentos_10_d, decodificador_7_segmentos_10_e, decodificador_7_segmentos_10_f,
       decodificador_7_segmentos_10_g, decodificador_7_segmentos_11_a, decodificador_7_segmentos_11_b,
       decodificador_7_segmentos_11_c, decodificador_7_segmentos_11_d, decodificador_7_segmentos_11_e,
       decodificador_7_segmentos_11_f, decodificador_7_segmentos_11_g, decodificador_7_segmentos_12_a,
       decodificador_7_segmentos_12_b, decodificador_7_segmentos_12_c, decodificador_7_segmentos_12_d,
       decodificador_7_segmentos_12_e, decodificador_7_segmentos_12_f, decodificador_7_segmentos_12_g,
       decodificador_7_segmentos_13_a, decodificador_7_segmentos_13_b, decodificador_7_segmentos_13_c,
       decodificador_7_segmentos_13_d, decodificador_7_segmentos_13_e, decodificador_7_segmentos_13_f,
       decodificador_7_segmentos_13_g, decodificador_7_segmentos_14_a, decodificador_7_segmentos_14_b,
       decodificador_7_segmentos_14_c, decodificador_7_segmentos_14_d, decodificador_7_segmentos_14_e,
       decodificador_7_segmentos_14_f, decodificador_7_segmentos_14_g, decodificador_7_segmentos_15_a,
       decodificador_7_segmentos_15_b, decodificador_7_segmentos_15_c, decodificador_7_segmentos_15_d,
       decodificador_7_segmentos_15_e, decodificador_7_segmentos_15_f, decodificador_7_segmentos_15_g,
       decodificador_7_segmentos_16_a, decodificador_7_segmentos_16_b, decodificador_7_segmentos_16_c,
       decodificador_7_segmentos_16_d, decodificador_7_segmentos_16_e, decodificador_7_segmentos_16_f,
       decodificador_7_segmentos_16_g, Reset_del_divisor_out, sumador_de_12_bits_1_overflow,
       union_7_leds_1_out_2, union_7_leds_1_out_3, union_7_leds_1_out_4, union_7_leds_1_out_5,
       union_7_leds_1_out_6, union_7_leds_1_out_7, union_7_leds_1_out_8, union_7_leds_1_out_9,
       union_7_leds_1_out_10, union_7_leds_1_out_11, union_7_leds_1_out_12, union_7_leds_1_out_13,
       union_7_leds_1_out_14, union_7_leds_1_out_15, union_7_leds_1_out_16, union_7_leds_1_out_17,
       union_7_leds_2_out_2, union_7_leds_2_out_3, union_7_leds_2_out_4, union_7_leds_2_out_5,
       union_7_leds_2_out_6, union_7_leds_2_out_7, union_7_leds_2_out_8, union_7_leds_2_out_9,
       union_7_leds_2_out_10, union_7_leds_2_out_11, union_7_leds_2_out_12, union_7_leds_2_out_13,
       union_7_leds_2_out_14, union_7_leds_2_out_15, union_7_leds_2_out_16, union_7_leds_2_out_17,
       union_7_leds_3_out_2, union_7_leds_3_out_3, union_7_leds_3_out_4, union_7_leds_3_out_5,
       union_7_leds_3_out_6, union_7_leds_3_out_7, union_7_leds_3_out_8, union_7_leds_3_out_9,
       union_7_leds_3_out_10, union_7_leds_3_out_11, union_7_leds_3_out_12, union_7_leds_3_out_13,
       union_7_leds_3_out_14, union_7_leds_3_out_15, union_7_leds_3_out_16, union_7_leds_3_out_17,
       union_7_leds_4_out_2, union_7_leds_4_out_3, union_7_leds_4_out_4, union_7_leds_4_out_5,
       union_7_leds_4_out_6, union_7_leds_4_out_7, union_7_leds_4_out_8, union_7_leds_4_out_9,
       union_7_leds_4_out_10, union_7_leds_4_out_11, union_7_leds_4_out_12, union_7_leds_4_out_13,
       union_7_leds_4_out_14, union_7_leds_4_out_15, union_7_leds_4_out_16, union_7_leds_4_out_17;
  wire [11:0] Complemento_a_la_base_out_2, demultiplexer_1_out0, demultiplexer_1_out1, demultiplexer_1_out3,
       demultiplexer_1_out4, demultiplexer_1_out5, demultiplexer_1_out6, demultiplexer_2_out0,
       demultiplexer_2_out2, demultiplexer_2_out3, demultiplexer_2_out4, demultiplexer_2_out5,
       demultiplexer_2_out6, Divisor_out_4, multiplexer_1_out, multiplexer_2_out, multiplexer_3_out,
       multiplexer_4_out, multiplexer_5_out, Multiplicador_out_3, sumador_de_12_bits_1_out_4;

  Union_7_Leds union_7_leds_1 (
    .in_1(in_1), .out_2(union_7_leds_1_out_2), .out_3(union_7_leds_1_out_3), .out_4(union_7_leds_1_out_4),
    .out_5(union_7_leds_1_out_5), .out_6(union_7_leds_1_out_6), .out_7(union_7_leds_1_out_7),
    .out_8(union_7_leds_1_out_8), .out_9(union_7_leds_1_out_9), .out_10(union_7_leds_1_out_10),
    .out_11(union_7_leds_1_out_11), .out_12(union_7_leds_1_out_12), .out_13(union_7_leds_1_out_13),
    .out_14(union_7_leds_1_out_14), .out_15(union_7_leds_1_out_15), .out_16(union_7_leds_1_out_16),
    .out_17(union_7_leds_1_out_17));
  Union_7_Leds union_7_leds_2 (
    .in_1(in_4), .out_2(union_7_leds_2_out_2), .out_3(union_7_leds_2_out_3), .out_4(union_7_leds_2_out_4),
    .out_5(union_7_leds_2_out_5), .out_6(union_7_leds_2_out_6), .out_7(union_7_leds_2_out_7),
    .out_8(union_7_leds_2_out_8), .out_9(union_7_leds_2_out_9), .out_10(union_7_leds_2_out_10),
    .out_11(union_7_leds_2_out_11), .out_12(union_7_leds_2_out_12), .out_13(union_7_leds_2_out_13),
    .out_14(union_7_leds_2_out_14), .out_15(union_7_leds_2_out_15), .out_16(union_7_leds_2_out_16),
    .out_17(union_7_leds_2_out_17));
  Multiplexer #(.width(12)) multiplexer_1 (
    .in0(in_1), .in1(in_4), .out(multiplexer_1_out), .sel(Invertir_entradas), .en(1'b1));
  Multiplexer #(.width(12)) multiplexer_2 (
    .in0(in_4), .in1(in_1), .out(multiplexer_2_out), .sel(Invertir_entradas), .en(1'b1));
  Demultiplexer #(.select(3), .width(12)) demultiplexer_1 (
    .out0(demultiplexer_1_out0), .out1(demultiplexer_1_out1), .out3(demultiplexer_1_out3),
    .out4(demultiplexer_1_out4), .out5(demultiplexer_1_out5), .out6(demultiplexer_1_out6),
    .in(multiplexer_1_out), .sel(\Selector_de_función ), .en(1'b1));  // open: out2, out7
  Demultiplexer #(.select(3), .width(12)) demultiplexer_2 (
    .out0(demultiplexer_2_out0), .out2(demultiplexer_2_out2), .out3(demultiplexer_2_out3),
    .out4(demultiplexer_2_out4), .out5(demultiplexer_2_out5), .out6(demultiplexer_2_out6),
    .in(multiplexer_2_out), .sel(\Selector_de_función ), .en(1'b1));  // open: out1, out7
  Button Reset_del_divisor (.out(Reset_del_divisor_out));
  Decodificador_7_Segmentos decodificador_7_segmentos_1 (
    .W(union_7_leds_1_out_14), .X(union_7_leds_1_out_15), .Y(union_7_leds_1_out_16),
    .Z(union_7_leds_1_out_17), .a(decodificador_7_segmentos_1_a), .b(decodificador_7_segmentos_1_b),
    .c(decodificador_7_segmentos_1_c), .d(decodificador_7_segmentos_1_d), .e(decodificador_7_segmentos_1_e),
    .f(decodificador_7_segmentos_1_f), .g(decodificador_7_segmentos_1_g));
  Decodificador_7_Segmentos decodificador_7_segmentos_2 (
    .W(union_7_leds_1_out_10), .X(union_7_leds_1_out_11), .Y(union_7_leds_1_out_12),
    .Z(union_7_leds_1_out_13), .a(decodificador_7_segmentos_2_a), .b(decodificador_7_segmentos_2_b),
    .c(decodificador_7_segmentos_2_c), .d(decodificador_7_segmentos_2_d), .e(decodificador_7_segmentos_2_e),
    .f(decodificador_7_segmentos_2_f), .g(decodificador_7_segmentos_2_g));
  Decodificador_7_Segmentos decodificador_7_segmentos_3 (
    .W(union_7_leds_1_out_6), .X(union_7_leds_1_out_7), .Y(union_7_leds_1_out_8), .Z(union_7_leds_1_out_9),
    .a(decodificador_7_segmentos_3_a), .b(decodificador_7_segmentos_3_b), .c(decodificador_7_segmentos_3_c),
    .d(decodificador_7_segmentos_3_d), .e(decodificador_7_segmentos_3_e), .f(decodificador_7_segmentos_3_f),
    .g(decodificador_7_segmentos_3_g));
  Decodificador_7_Segmentos decodificador_7_segmentos_4 (
    .W(union_7_leds_1_out_2), .X(union_7_leds_1_out_3), .Y(union_7_leds_1_out_4), .Z(union_7_leds_1_out_5),
    .a(decodificador_7_segmentos_4_a), .b(decodificador_7_segmentos_4_b), .c(decodificador_7_segmentos_4_c),
    .d(decodificador_7_segmentos_4_d), .e(decodificador_7_segmentos_4_e), .f(decodificador_7_segmentos_4_f),
    .g(decodificador_7_segmentos_4_g));
  Decodificador_7_Segmentos decodificador_7_segmentos_5 (
    .W(union_7_leds_2_out_14), .X(union_7_leds_2_out_15), .Y(union_7_leds_2_out_16),
    .Z(union_7_leds_2_out_17), .a(decodificador_7_segmentos_5_a), .b(decodificador_7_segmentos_5_b),
    .c(decodificador_7_segmentos_5_c), .d(decodificador_7_segmentos_5_d), .e(decodificador_7_segmentos_5_e),
    .f(decodificador_7_segmentos_5_f), .g(decodificador_7_segmentos_5_g));
  Decodificador_7_Segmentos decodificador_7_segmentos_6 (
    .W(union_7_leds_2_out_10), .X(union_7_leds_2_out_11), .Y(union_7_leds_2_out_12),
    .Z(union_7_leds_2_out_13), .a(decodificador_7_segmentos_6_a), .b(decodificador_7_segmentos_6_b),
    .c(decodificador_7_segmentos_6_c), .d(decodificador_7_segmentos_6_d), .e(decodificador_7_segmentos_6_e),
    .f(decodificador_7_segmentos_6_f), .g(decodificador_7_segmentos_6_g));
  Decodificador_7_Segmentos decodificador_7_segmentos_7 (
    .W(union_7_leds_2_out_6), .X(union_7_leds_2_out_7), .Y(union_7_leds_2_out_8), .Z(union_7_leds_2_out_9),
    .a(decodificador_7_segmentos_7_a), .b(decodificador_7_segmentos_7_b), .c(decodificador_7_segmentos_7_c),
    .d(decodificador_7_segmentos_7_d), .e(decodificador_7_segmentos_7_e), .f(decodificador_7_segmentos_7_f),
    .g(decodificador_7_segmentos_7_g));
  Decodificador_7_Segmentos decodificador_7_segmentos_8 (
    .W(union_7_leds_2_out_2), .X(union_7_leds_2_out_3), .Y(union_7_leds_2_out_4), .Z(union_7_leds_2_out_5),
    .a(decodificador_7_segmentos_8_a), .b(decodificador_7_segmentos_8_b), .c(decodificador_7_segmentos_8_c),
    .d(decodificador_7_segmentos_8_d), .e(decodificador_7_segmentos_8_e), .f(decodificador_7_segmentos_8_f),
    .g(decodificador_7_segmentos_8_g));
  Multiplexer #(.select(3), .width(12)) multiplexer_3 (
    .in1(demultiplexer_1_out1), .in2(demultiplexer_2_out2), .in3(demultiplexer_2_out3),
    .out(multiplexer_3_out), .sel(\Selector_de_función ), .en(1'b1));  // open: in0, in4, in5, in6, in7
  _7_Segment_Display u_7_segment_display_1 (
    .g(decodificador_7_segmentos_1_g), .f(decodificador_7_segmentos_1_f), .a(decodificador_7_segmentos_1_a),
    .b(decodificador_7_segmentos_1_b), .e(decodificador_7_segmentos_1_e), .d(decodificador_7_segmentos_1_d),
    .c(decodificador_7_segmentos_1_c));  // open: dp
  Multiplexer #(.select(3), .width(12)) multiplexer_4 (
    .in0(demultiplexer_1_out0), .in3(demultiplexer_1_out3), .out(multiplexer_4_out),
    .sel(\Selector_de_función ), .en(1'b1));  // open: in1, in2, in4, in5, in6, in7
  complemento_a_base_2__12_bits Complemento_a_la_base (
    .in_1(multiplexer_3_out), .out_2(Complemento_a_la_base_out_2), .out_3(Complemento_a_la_base_out_3));
  multiplicador Multiplicador (
    .in_1(demultiplexer_1_out4), .in_2(demultiplexer_2_out4), .out_3(Multiplicador_out_3), .out_4(Salida_D));
  divisor Divisor (
    .in_1(demultiplexer_1_out5), .in_2(demultiplexer_2_out5), .out_4(Divisor_out_4),
    .in_3(Reset_del_divisor_out));
  _7_Segment_Display u_7_segment_display_2 (
    .g(decodificador_7_segmentos_5_g), .f(decodificador_7_segmentos_5_f), .a(decodificador_7_segmentos_5_a),
    .b(decodificador_7_segmentos_5_b), .e(decodificador_7_segmentos_5_e), .d(decodificador_7_segmentos_5_d),
    .c(decodificador_7_segmentos_5_c));  // open: dp
  _7_Segment_Display u_7_segment_display_3 (
    .g(decodificador_7_segmentos_2_g), .f(decodificador_7_segmentos_2_f), .a(decodificador_7_segmentos_2_a),
    .b(decodificador_7_segmentos_2_b), .e(decodificador_7_segmentos_2_e), .d(decodificador_7_segmentos_2_d),
    .c(decodificador_7_segmentos_2_c));  // open: dp
  Multiplexer #(.select(3), .width(12)) multiplexer_5 (
    .in0(demultiplexer_2_out0), .in3(Complemento_a_la_base_out_2), .out(multiplexer_5_out),
    .sel(\Selector_de_función ), .en(1'b1));  // open: in1, in2, in4, in5, in6, in7
  _7_Segment_Display u_7_segment_display_4 (
    .g(decodificador_7_segmentos_6_g), .f(decodificador_7_segmentos_6_f), .a(decodificador_7_segmentos_6_a),
    .b(decodificador_7_segmentos_6_b), .e(decodificador_7_segmentos_6_e), .d(decodificador_7_segmentos_6_d),
    .c(decodificador_7_segmentos_6_c));  // open: dp
  _7_Segment_Display u_7_segment_display_5 (
    .g(decodificador_7_segmentos_3_g), .f(decodificador_7_segmentos_3_f), .a(decodificador_7_segmentos_3_a),
    .b(decodificador_7_segmentos_3_b), .e(decodificador_7_segmentos_3_e), .d(decodificador_7_segmentos_3_d),
    .c(decodificador_7_segmentos_3_c));  // open: dp
  sumador_de_12_bits sumador_de_12_bits_1 (
    .entrada_A(multiplexer_4_out), .entrada_B(multiplexer_5_out), .out_4(sumador_de_12_bits_1_out_4),
    .Overflow(sumador_de_12_bits_1_overflow), .in_1(1'b0));
  _7_Segment_Display u_7_segment_display_6 (
    .g(decodificador_7_segmentos_7_g), .f(decodificador_7_segmentos_7_f), .a(decodificador_7_segmentos_7_a),
    .b(decodificador_7_segmentos_7_b), .e(decodificador_7_segmentos_7_e), .d(decodificador_7_segmentos_7_d),
    .c(decodificador_7_segmentos_7_c));  // open: dp
  _7_Segment_Display u_7_segment_display_7 (
    .g(decodificador_7_segmentos_4_g), .f(decodificador_7_segmentos_4_f), .a(decodificador_7_segmentos_4_a),
    .b(decodificador_7_segmentos_4_b), .e(decodificador_7_segmentos_4_e), .d(decodificador_7_segmentos_4_d),
    .c(decodificador_7_segmentos_4_c));  // open: dp
  Multiplexer #(.select(3), .width(12)) multiplexer_6 (
    .in0(sumador_de_12_bits_1_out_4), .in1(Complemento_a_la_base_out_2), .in2(Complemento_a_la_base_out_2),
    .in3(sumador_de_12_bits_1_out_4), .in4(Multiplicador_out_3), .in5(Divisor_out_4), .out(Salida_C[11:0]),
    .sel(\Selector_de_función ), .en(1'b1));  // open: in6, in7
  LED led_1 (.in(Comparador_a_b));
  comparador Comparador (
    .in_1(demultiplexer_1_out6), .in_2(demultiplexer_2_out6), .A__B(Comparador_a__b),
    .A__B_2(Comparador_a__b_2), .A_B(Comparador_a_b));
  LED led_2 (.in(Comparador_a__b_2));
  LED led_3 (.in(Comparador_a__b));
  _7_Segment_Display u_7_segment_display_8 (
    .g(decodificador_7_segmentos_8_g), .f(decodificador_7_segmentos_8_f), .a(decodificador_7_segmentos_8_a),
    .b(decodificador_7_segmentos_8_b), .e(decodificador_7_segmentos_8_e), .d(decodificador_7_segmentos_8_d),
    .c(decodificador_7_segmentos_8_c));  // open: dp
  Multiplexer #(.select(3)) multiplexer_7 (
    .in0(sumador_de_12_bits_1_overflow), .in1(Complemento_a_la_base_out_3),
    .in2(Complemento_a_la_base_out_3), .in3(sumador_de_12_bits_1_overflow), .out(Salida_C[12]),
    .sel(\Selector_de_función ), .en(1'b1));  // open: in4, in5, in6, in7
  Union_7_Leds union_7_leds_3 (
    .in_1(Salida_C[11:0]), .out_2(union_7_leds_3_out_2), .out_3(union_7_leds_3_out_3),
    .out_4(union_7_leds_3_out_4), .out_5(union_7_leds_3_out_5), .out_6(union_7_leds_3_out_6),
    .out_7(union_7_leds_3_out_7), .out_8(union_7_leds_3_out_8), .out_9(union_7_leds_3_out_9),
    .out_10(union_7_leds_3_out_10), .out_11(union_7_leds_3_out_11), .out_12(union_7_leds_3_out_12),
    .out_13(union_7_leds_3_out_13), .out_14(union_7_leds_3_out_14), .out_15(union_7_leds_3_out_15),
    .out_16(union_7_leds_3_out_16), .out_17(union_7_leds_3_out_17));
  Union_7_Leds union_7_leds_4 (
    .in_1(Salida_D), .out_2(union_7_leds_4_out_2), .out_3(union_7_leds_4_out_3),
    .out_4(union_7_leds_4_out_4), .out_5(union_7_leds_4_out_5), .out_6(union_7_leds_4_out_6),
    .out_7(union_7_leds_4_out_7), .out_8(union_7_leds_4_out_8), .out_9(union_7_leds_4_out_9),
    .out_10(union_7_leds_4_out_10), .out_11(union_7_leds_4_out_11), .out_12(union_7_leds_4_out_12),
    .out_13(union_7_leds_4_out_13), .out_14(union_7_leds_4_out_14), .out_15(union_7_leds_4_out_15),
    .out_16(union_7_leds_4_out_16), .out_17(union_7_leds_4_out_17));
  Decodificador_7_Segmentos decodificador_7_segmentos_9 (
    .W(union_7_leds_3_out_14), .X(union_7_leds_3_out_15), .Y(union_7_leds_3_out_16),
    .Z(union_7_leds_3_out_17), .a(decodificador_7_segmentos_9_a), .b(decodificador_7_segmentos_9_b),
    .c(decodificador_7_segmentos_9_c), .d(decodificador_7_segmentos_9_d), .e(decodificador_7_segmentos_9_e),
    .f(decodificador_7_segmentos_9_f), .g(decodificador_7_segmentos_9_g));
  Decodificador_7_Segmentos decodificador_7_segmentos_10 (
    .W(union_7_leds_3_out_10), .X(union_7_leds_3_out_11), .Y(union_7_leds_3_out_12),
    .Z(union_7_leds_3_out_13), .a(decodificador_7_segmentos_10_a), .b(decodificador_7_segmentos_10_b),
    .c(decodificador_7_segmentos_10_c), .d(decodificador_7_segmentos_10_d),
    .e(decodificador_7_segmentos_10_e), .f(decodificador_7_segmentos_10_f), .g(decodificador_7_segmentos_10_g));
  Decodificador_7_Segmentos decodificador_7_segmentos_11 (
    .W(union_7_leds_3_out_6), .X(union_7_leds_3_out_7), .Y(union_7_leds_3_out_8), .Z(union_7_leds_3_out_9),
    .a(decodificador_7_segmentos_11_a), .b(decodificador_7_segmentos_11_b),
    .c(decodificador_7_segmentos_11_c), .d(decodificador_7_segmentos_11_d),
    .e(decodificador_7_segmentos_11_e), .f(decodificador_7_segmentos_11_f), .g(decodificador_7_segmentos_11_g));
  Decodificador_7_Segmentos decodificador_7_segmentos_12 (
    .W(union_7_leds_3_out_2), .X(union_7_leds_3_out_3), .Y(union_7_leds_3_out_4), .Z(union_7_leds_3_out_5),
    .a(decodificador_7_segmentos_12_a), .b(decodificador_7_segmentos_12_b),
    .c(decodificador_7_segmentos_12_c), .d(decodificador_7_segmentos_12_d),
    .e(decodificador_7_segmentos_12_e), .f(decodificador_7_segmentos_12_f), .g(decodificador_7_segmentos_12_g));
  Decodificador_7_Segmentos decodificador_7_segmentos_13 (
    .W(union_7_leds_4_out_14), .X(union_7_leds_4_out_15), .Y(union_7_leds_4_out_16),
    .Z(union_7_leds_4_out_17), .a(decodificador_7_segmentos_13_a), .b(decodificador_7_segmentos_13_b),
    .c(decodificador_7_segmentos_13_c), .d(decodificador_7_segmentos_13_d),
    .e(decodificador_7_segmentos_13_e), .f(decodificador_7_segmentos_13_f), .g(decodificador_7_segmentos_13_g));
  Decodificador_7_Segmentos decodificador_7_segmentos_14 (
    .W(union_7_leds_4_out_10), .X(union_7_leds_4_out_11), .Y(union_7_leds_4_out_12),
    .Z(union_7_leds_4_out_13), .a(decodificador_7_segmentos_14_a), .b(decodificador_7_segmentos_14_b),
    .c(decodificador_7_segmentos_14_c), .d(decodificador_7_segmentos_14_d),
    .e(decodificador_7_segmentos_14_e), .f(decodificador_7_segmentos_14_f), .g(decodificador_7_segmentos_14_g));
  Decodificador_7_Segmentos decodificador_7_segmentos_15 (
    .W(union_7_leds_4_out_6), .X(union_7_leds_4_out_7), .Y(union_7_leds_4_out_8), .Z(union_7_leds_4_out_9),
    .a(decodificador_7_segmentos_15_a), .b(decodificador_7_segmentos_15_b),
    .c(decodificador_7_segmentos_15_c), .d(decodificador_7_segmentos_15_d),
    .e(decodificador_7_segmentos_15_e), .f(decodificador_7_segmentos_15_f), .g(decodificador_7_segmentos_15_g));
  Decodificador_7_Segmentos decodificador_7_segmentos_16 (
    .W(union_7_leds_4_out_2), .X(union_7_leds_4_out_3), .Y(union_7_leds_4_out_4), .Z(union_7_leds_4_out_5),
    .a(decodificador_7_segmentos_16_a), .b(decodificador_7_segmentos_16_b),
    .c(decodificador_7_segmentos_16_c), .d(decodificador_7_segmentos_16_d),
    .e(decodificador_7_segmentos_16_e), .f(decodificador_7_segmentos_16_f), .g(decodificador_7_segmentos_16_g));
  _7_Segment_Display u_7_segment_display_9 (
    .g(decodificador_7_segmentos_9_g), .f(decodificador_7_segmentos_9_f), .a(decodificador_7_segmentos_9_a),
    .b(decodificador_7_segmentos_9_b), .e(decodificador_7_segmentos_9_e), .d(decodificador_7_segmentos_9_d),
    .c(decodificador_7_segmentos_9_c));  // open: dp
  _7_Segment_Display u_7_segment_display_10 (
    .g(decodificador_7_segmentos_13_g), .f(decodificador_7_segmentos_13_f),
    .a(decodificador_7_segmentos_13_a), .b(decodificador_7_segmentos_13_b),
    .e(decodificador_7_segmentos_13_e), .d(decodificador_7_segmentos_13_d), .c(decodificador_7_segmentos_13_c));  // open: dp
  _7_Segment_Display u_7_segment_display_11 (
    .g(decodificador_7_segmentos_10_g), .f(decodificador_7_segmentos_10_f),
    .a(decodificador_7_segmentos_10_a), .b(decodificador_7_segmentos_10_b),
    .e(decodificador_7_segmentos_10_e), .d(decodificador_7_segmentos_10_d), .c(decodificador_7_segmentos_10_c));  // open: dp
  _7_Segment_Display u_7_segment_display_12 (
    .g(decodificador_7_segmentos_14_g), .f(decodificador_7_segmentos_14_f),
    .a(decodificador_7_segmentos_14_a), .b(decodificador_7_segmentos_14_b),
    .e(decodificador_7_segmentos_14_e), .d(decodificador_7_segmentos_14_d), .c(decodificador_7_segmentos_14_c));  // open: dp
  _7_Segment_Display u_7_segment_display_13 (
    .g(decodificador_7_segmentos_11_g), .f(decodificador_7_segmentos_11_f),
    .a(decodificador_7_segmentos_11_a), .b(decodificador_7_segmentos_11_b),
    .e(decodificador_7_segmentos_11_e), .d(decodificador_7_segmentos_11_d), .c(decodificador_7_segmentos_11_c));  // open: dp
  _7_Segment_Display u_7_segment_display_14 (
    .g(decodificador_7_segmentos_15_g), .f(decodificador_7_segmentos_15_f),
    .a(decodificador_7_segmentos_15_a), .b(decodificador_7_segmentos_15_b),
    .e(decodificador_7_segmentos_15_e), .d(decodificador_7_segmentos_15_d), .c(decodificador_7_segmentos_15_c));  // open: dp
  _7_Segment_Display u_7_segment_display_15 (
    .g(decodificador_7_segmentos_12_g), .f(decodificador_7_segmentos_12_f),
    .a(decodificador_7_segmentos_12_a), .b(decodificador_7_segmentos_12_b),
    .e(decodificador_7_segmentos_12_e), .d(decodificador_7_segmentos_12_d), .c(decodificador_7_segmentos_12_c));  // open: dp
  _7_Segment_Display u_7_segment_display_16 (
    .g(decodificador_7_segmentos_16_g), .f(decodificador_7_segmentos_16_f),
    .a(decodificador_7_segmentos_16_a), .b(decodificador_7_segmentos_16_b),
    .e(decodificador_7_segmentos_16_e), .d(decodificador_7_segmentos_16_d), .c(decodificador_7_segmentos_16_c));  // open: dp
endmodule

module divisor (
  input  [11:0] in_1,
  input  [11:0] in_2,
  input  in_3,
  output [11:0] out_4
);

  wire clock_1_out, comparador_1_a__b, comparador_2_a_b, controlled_buffer_2_out,
       sumador_de_12_bits_1_overflow, xor_1_out;
  wire [11:0] controlled_buffer_1_out, register_1_q;

  comparador comparador_1 (.in_1(register_1_q), .in_2({12{1'b0}}), .A__B(comparador_1_a__b));  // open: A__B_2, A_B
  assign controlled_buffer_1_out = comparador_1_a__b ? in_2 : 12'bz;  // Controlled_Buffer controlled_buffer_1
  Register #(.width(12)) register_1 (
    .D(controlled_buffer_1_out), .Q(register_1_q), .clk(controlled_buffer_2_out), .clr(in_3));  // open: en
  comparador comparador_2 (.in_1(in_1), .in_2(register_1_q), .A_B(comparador_2_a_b));  // open: A__B, A__B_2
  sumador_de_12_bits sumador_de_12_bits_1 (
    .entrada_A(register_1_q), .entrada_B(in_2), .out_4(controlled_buffer_1_out),
    .Overflow(sumador_de_12_bits_1_overflow), .in_1(1'b0));
  xor xor_1 (xor_1_out, sumador_de_12_bits_1_overflow, comparador_2_a_b);
  assign controlled_buffer_2_out = xor_1_out ? clock_1_out : 1'bz;  // Controlled_Buffer controlled_buffer_2
  Clock clock_1 (.out(clock_1_out));
  Counter #(.width(12), .max('hfff)) counter_1 (
    .Q(out_4), .clk(controlled_buffer_2_out), .clr(in_3));  // open: load, D, count, carry
endmodule

module multiplicador (
  input  [11:0] in_1,
  input  [11:0] in_2,
  output [11:0] out_3,
  output [11:0] out_4
);

  wire clock_1_out, comparador_1_a__b, comparador_2_a__b, controlled_buffer_2_out, counter_1_carry,
       not_1_out, sumador_de_12_bits_1_overflow;
  wire [11:0] counter_1_q;
  wire [23:0] bit_extender_1_out, controlled_buffer_1_out;

  Counter #(.width(12), .max('hfff)) counter_1 (
    .Q(counter_1_q), .carry(counter_1_carry), .clk(controlled_buffer_2_out), .clr(counter_1_carry));  // open: load, D, count
  comparador comparador_1 (.in_1(counter_1_q), .in_2({12{1'b0}}), .A__B(comparador_1_a__b));  // open: A__B_2, A_B
  assign bit_extender_1_out = {{12{1'b0}}, in_1};  // Bit_Extender bit_extender_1
  comparador comparador_2 (.in_1(in_2), .in_2(counter_1_q), .A__B(comparador_2_a__b));  // open: A__B_2, A_B
  assign controlled_buffer_1_out = comparador_1_a__b ? bit_extender_1_out : 24'bz;  // Controlled_Buffer controlled_buffer_1
  assign controlled_buffer_2_out = not_1_out ? clock_1_out : 1'bz;  // Controlled_Buffer controlled_buffer_2
  not not_1 (not_1_out, comparador_2_a__b);
  Clock clock_1 (.out(clock_1_out));
  Register #(.width(24)) register_1 (
    .D(controlled_buffer_1_out), .Q({out_4, out_3}), .clk(controlled_buffer_2_out), .clr(counter_1_carry));  // open: en
  sumador_de_12_bits sumador_de_12_bits_1 (
    .entrada_A(out_3), .entrada_B(in_1), .out_4(controlled_buffer_1_out[11:0]),
    .Overflow(sumador_de_12_bits_1_overflow), .in_1(1'b0));
  sumador_de_12_bits sumador_de_12_bits_2 (
    .entrada_A(out_4), .entrada_B({12{1'b0}}), .out_4(controlled_buffer_1_out[23:12]),
    .in_1(sumador_de_12_bits_1_overflow));  // open: Overflow
endmodule

module Contador_12_Bits (
  input  in_1,
  input  in_2,
  output [11:0] out_3
);

  wire j_k_ff_1_qn, j_k_ff_2_qn, j_k_ff_3_qn, j_k_ff_4_qn, j_k_ff_5_qn, j_k_ff_6_qn, j_k_ff_7_qn,
       j_k_ff_9_qn, j_k_ff_10_qn, j_k_ff_11_qn, j_k_ff_12_qn;

  J_K_Flip_Flop j_k_ff_1 (.J(in_1), .clk(in_2), .K(in_1), .Q(out_3[0]), .Qn(j_k_ff_1_qn));  // open: preset, en, reset
  J_K_Flip_Flop j_k_ff_2 (
    .J(in_1), .clk(j_k_ff_12_qn), .K(in_1), .Q(out_3[8]), .Qn(j_k_ff_2_qn));  // open: preset, en, reset
  J_K_Flip_Flop j_k_ff_3 (
    .J(in_1), .clk(j_k_ff_1_qn), .K(in_1), .Q(out_3[1]), .Qn(j_k_ff_3_qn));  // open: preset, en, reset
  J_K_Flip_Flop j_k_ff_4 (
    .J(in_1), .clk(j_k_ff_2_qn), .K(in_1), .Q(out_3[9]), .Qn(j_k_ff_4_qn));  // open: preset, en, reset
  J_K_Flip_Flop j_k_ff_5 (
    .J(in_1), .clk(j_k_ff_3_qn), .K(in_1), .Q(out_3[2]), .Qn(j_k_ff_5_qn));  // open: preset, en, reset
  J_K_Flip_Flop j_k_ff_6 (
    .J(in_1), .clk(j_k_ff_4_qn), .K(in_1), .Q(out_3[10]), .Qn(j_k_ff_6_qn));  // open: preset, en, reset
  J_K_Flip_Flop j_k_ff_7 (
    .J(in_1), .clk(j_k_ff_5_qn), .K(in_1), .Q(out_3[3]), .Qn(j_k_ff_7_qn));  // open: preset, en, reset
  J_K_Flip_Flop j_k_ff_8 (.J(in_1), .clk(j_k_ff_6_qn), .K(in_1), .Q(out_3[11]));  // open: Qn, preset, en, reset
  J_K_Flip_Flop j_k_ff_9 (
    .J(in_1), .clk(j_k_ff_7_qn), .K(in_1), .Q(out_3[4]), .Qn(j_k_ff_9_qn));  // open: preset, en, reset
  J_K_Flip_Flop j_k_ff_10 (
    .J(in_1), .clk(j_k_ff_9_qn), .K(in_1), .Q(out_3[5]), .Qn(j_k_ff_10_qn));  // open: preset, en, reset
  J_K_Flip_Flop j_k_ff_11 (
    .J(in_1), .clk(j_k_ff_10_qn), .K(in_1), .Q(out_3[6]), .Qn(j_k_ff_11_qn));  // open: preset, en, reset
  J_K_Flip_Flop j_k_ff_12 (
    .J(in_1), .clk(j_k_ff_11_qn), .K(in_1), .Q(out_3[7]), .Qn(j_k_ff_12_qn));  // open: preset, en, reset
endmodule

module Contador_Numero_Decimal (
  input  in_1,
  input  in_2,
  output out_3,
  output out_4,
  output out_5,
  output out_6,
  output out_7
);

  wire and_1_out, and_2_out, j_k_ff_2_qn, j_k_ff_3_qn, j_k_ff_4_qn, not_1_out;

  not not_1 (not_1_out, in_2);
  and and_1 (and_1_out, not_1_out, out_7);
  J_K_Flip_Flop j_k_ff_1 (.J(in_1), .clk(and_2_out), .K(in_1), .Q(out_7), .reset(and_1_out));  // open: Qn, preset, en
  and and_2 (and_2_out, out_3, out_5);
  J_K_Flip_Flop j_k_ff_2 (
    .J(in_1), .clk(in_2), .K(in_1), .Q(out_6), .Qn(j_k_ff_2_qn), .reset(and_2_out));  // open: preset, en
  J_K_Flip_Flop j_k_ff_3 (
    .J(in_1), .clk(j_k_ff_2_qn), .K(in_1), .Q(out_5), .Qn(j_k_ff_3_qn), .reset(and_2_out));  // open: preset, en
  J_K_Flip_Flop j_k_ff_4 (
    .J(in_1), .clk(j_k_ff_3_qn), .K(in_1), .Q(out_4), .Qn(j_k_ff_4_qn), .reset(and_2_out));  // open: preset, en
  J_K_Flip_Flop j_k_ff_5 (.J(in_1), .clk(j_k_ff_4_qn), .K(in_1), .Q(out_3), .reset(and_2_out));  // open: Qn, preset, en
endmodule

module Decodificador_7_Segmentos (
  input  W,
  input  X,
  input  Y,
  input  Z,
  output a,
  output b,
  output c,
  output d,
  output e,
  output f,
  output g
);

  wire and_1_out, and_2_out, and_3_out, and_4_out, and_5_out, and_6_out, and_7_out, and_8_out, and_9_out,
       and_10_out, and_11_out, and_12_out, and_13_out, and_14_out, and_15_out, and_16_out, not_1_out,
       not_2_out, not_3_out, not_4_out, not_5_out, not_6_out, not_7_out, not_8_out, not_9_out, not_10_out,
       not_11_out, not_12_out, not_13_out, not_14_out, not_15_out, not_16_out, not_17_out, not_18_out,
       not_19_out, not_20_out, not_21_out;

  not not_1 (not_1_out, X);
  and and_1 (and_1_out, not_1_out, not_2_out);
  not not_2 (not_2_out, Z);
  and and_2 (and_2_out, X, Z);
  not not_3 (not_3_out, X);
  not not_4 (not_4_out, Y);
  and and_3 (and_3_out, not_4_out, not_5_out);
  not not_5 (not_5_out, Z);
  and and_4 (and_4_out, Y, Z);
  not not_6 (not_6_out, Y);
  or or_1 (c, not_6_out, Z, X);
  not not_7 (not_7_out, X);
  and and_5 (and_5_out, not_7_out, not_8_out);
  not not_8 (not_8_out, Z);
  not not_9 (not_9_out, X);
  and and_6 (and_6_out, not_9_out, Y);
  and and_7 (and_7_out, Y, not_10_out);
  not not_10 (not_10_out, Z);
  and and_8 (and_8_out, X, not_11_out, Z);
  not not_11 (not_11_out, Y);
  not not_12 (not_12_out, X);
  and and_9 (and_9_out, not_12_out, not_13_out);
  not not_13 (not_13_out, Z);
  and and_10 (and_10_out, Y, not_14_out);
  not not_14 (not_14_out, Z);
  not not_15 (not_15_out, Y);
  and and_11 (and_11_out, not_15_out, not_16_out);
  not not_16 (not_16_out, Z);
  and and_12 (and_12_out, X, not_17_out);
  not not_17 (not_17_out, Y);
  and and_13 (and_13_out, X, not_18_out);
  not not_18 (not_18_out, Z);
  not not_19 (not_19_out, X);
  and and_14 (and_14_out, not_19_out, Y);
  and and_15 (and_15_out, X, not_20_out);
  not not_20 (not_20_out, Y);
  and and_16 (and_16_out, X, not_21_out);
  not not_21 (not_21_out, Z);
  or or_2 (a, and_1_out, Y, and_2_out, W);
  or or_3 (b, not_3_out, and_3_out, and_4_out);
  or or_4 (d, and_5_out, and_6_out, and_7_out, and_8_out, W);
  or or_5 (e, and_9_out, and_10_out);
  or or_6 (f, and_11_out, and_12_out, and_13_out, W);
  or or_7 (g, and_14_out, and_15_out, and_16_out, W);
endmodule

module Union_7_Leds (
  input  [11:0] in_1,
  output out_2,
  output out_3,
  output out_4,
  output out_5,
  output out_6,
  output out_7,
  output out_8,
  output out_9,
  output out_10,
  output out_11,
  output out_12,
  output out_13,
  output out_14,
  output out_15,
  output out_16,
  output out_17
);

  wire and_1_out, clock_1_out, comparator_1_eq, contador_numero_decimal_1_out_7,
       contador_numero_decimal_2_out_7, contador_numero_decimal_3_out_7, not_1_out;
  wire [11:0] contador_12_bits_1_out_3;

  Contador_12_Bits contador_12_bits_1 (.in_1(and_1_out), .in_2(and_1_out), .out_3(contador_12_bits_1_out_3));
  Clock clock_1 (.out(clock_1_out));
  and and_1 (and_1_out, clock_1_out, not_1_out);
  not not_1 (not_1_out, comparator_1_eq);
  Comparator #(.width(12)) comparator_1 (.a(in_1), .b(contador_12_bits_1_out_3), .eq(comparator_1_eq));  // open: gt, lt
  Contador_Numero_Decimal contador_numero_decimal_1 (
    .in_1(and_1_out), .in_2(and_1_out), .out_3(out_2), .out_4(out_3), .out_5(out_4), .out_6(out_5),
    .out_7(contador_numero_decimal_1_out_7));
  Contador_Numero_Decimal contador_numero_decimal_2 (
    .in_1(contador_numero_decimal_1_out_7), .in_2(contador_numero_decimal_1_out_7), .out_3(out_6),
    .out_4(out_7), .out_5(out_8), .out_6(out_9), .out_7(contador_numero_decimal_2_out_7));
  Contador_Numero_Decimal contador_numero_decimal_3 (
    .in_1(contador_numero_decimal_2_out_7), .in_2(contador_numero_decimal_2_out_7), .out_3(out_10),
    .out_4(out_11), .out_5(out_12), .out_6(out_13), .out_7(contador_numero_decimal_3_out_7));
  Contador_Numero_Decimal contador_numero_decimal_4 (
    .in_1(contador_numero_decimal_3_out_7), .in_2(contador_numero_decimal_3_out_7), .out_3(out_14),
    .out_4(out_15), .out_5(out_16), .out_6(out_17));  // open: out_7
endmodule
